# Fritzing sketch board-mapping-fritzing (saved by Fritzing 0.9.3b)
breadboards: 1

parts:
  Part1 = Arduino Uno (Rev3)
  Part2 = Real Time Clock Module - DS1307 RTC Breakout Board
  J1 = Basic Servo

nets:
  N1: Part1.D9_PWM, J1.pulse
  N2: Part1.A4/SDA, Part2.SCL
  N3: Part1.A5/SCL, Part2.SDA
  N4: Part1.D2, Part2.SQW
  5V: Part1.5V, Part2.5V, J1.vcc
  GND: Part1.GND, Part2.GND, J1.gnd
